// Logisim project Trabalho M1.circ as structural Verilog: 8 circuits, main circuit main
module main (
  input  D3,
  input  D2,
  input  D1,
  input  D0
);

  wire a_1_out_5, b_1_out_5, c_1_out_5, d_1_out_5, e_1_out_5, f_1_out_5, g_1_out_5;

  A a_1 (.out_5(a_1_out_5), .D3(D3), .D2(D2), .D1(D1), .D0(D0));
  B b_1 (.out_5(b_1_out_5), .D3(D3), .D2(D2), .D1(D1), .D0(D0));
  C c_1 (.out_5(c_1_out_5), .D3(D3), .D2(D2), .D1(D1), .D0(D0));
  D d_1 (.out_5(d_1_out_5), .D3(D3), .D2(D2), .D1(D1), .D0(D0));
  E e_1 (.out_5(e_1_out_5), .D3(D3), .D2(D2), .D1(D1), .D0(D0));
  F f_1 (.out_5(f_1_out_5), .D3(D3), .D2(D2), .D1(D1), .D0(D0));
  G g_1 (.out_5(g_1_out_5), .D3(D3), .D2(D2), .D1(D1), .D0(D0));
  _7_Segment_Display u_7_segment_display_1 (
    .g(g_1_out_5), .f(f_1_out_5), .a(a_1_out_5), .b(b_1_out_5), .e(e_1_out_5), .d(d_1_out_5), .c(c_1_out_5));  // open: dp

  // Notes on the sheet:
  //   TRABALHO DE CIRCUITOS DIGITAIS.
  //   PROF:PAULO ROBERTO OLIVEIRA VALIM.
  //   ALUNOS:RAFAEL DA CUNHA, EDUARDO.
endmodule

module A (
  input  D3,
  input  D2,
  input  D1,
  input  D0,
  output out_5
);

  wire and_1_out, and_2_out, and_3_out;

  and and_1 (and_1_out, D2, ~D1);  // AND_Gate
  and and_2 (and_2_out, ~D3, ~D0);  // AND_Gate
  and and_3 (and_3_out, D3, ~D2, D1, D0);  // AND_Gate
  or or_1 (out_5, and_1_out, and_2_out, and_3_out);
endmodule

module B (
  input  D3,
  input  D2,
  input  D1,
  input  D0,
  output out_5
);

  wire and_1_out, and_2_out, and_3_out, and_4_out;

  and and_1 (and_1_out, D3, ~D1);  // AND_Gate
  and and_2 (and_2_out, D3, D2);
  and and_3 (and_3_out, D1, D0);
  and and_4 (and_4_out, ~D2, ~D1, ~D0);  // AND_Gate
  or or_1 (out_5, and_1_out, and_2_out, and_3_out, and_4_out);
endmodule

module C (
  input  D3,
  input  D2,
  input  D1,
  input  D0,
  output out_5
);

  wire and_1_out, and_2_out, and_3_out, and_4_out;

  and and_1 (and_1_out, D2, D1);
  and and_2 (and_2_out, D1, D0);
  and and_3 (and_3_out, ~D2, ~D1);  // AND_Gate
  and and_4 (and_4_out, D3, ~D1, ~D0);  // AND_Gate
  or or_1 (out_5, and_1_out, and_2_out, and_3_out, and_4_out);
endmodule

module D (
  input  D3,
  input  D2,
  input  D1,
  input  D0,
  output out_5
);

  wire and_1_out, and_2_out, and_3_out, and_4_out, and_5_out;

  and and_1 (and_1_out, D2, ~D0);  // AND_Gate
  and and_2 (and_2_out, D1, ~D0);  // AND_Gate
  and and_3 (and_3_out, D3, D2, D1);
  and and_4 (and_4_out, ~D3, ~D2, D0);  // AND_Gate
  and and_5 (and_5_out, ~D2, ~D1, D0);  // AND_Gate
  or or_1 (out_5, and_1_out, and_2_out, and_3_out, and_4_out, and_5_out);
endmodule

module E (
  input  D3,
  input  D2,
  input  D1,
  input  D0,
  output out_5
);

  wire and_1_out, and_2_out, and_3_out;

  and and_1 (and_1_out, D2, ~D1);  // AND_Gate
  and and_2 (and_2_out, ~D2, D0);  // AND_Gate
  and and_3 (and_3_out, D1, ~D0);  // AND_Gate
  or or_1 (out_5, ~D3, and_1_out, and_2_out, and_3_out);  // OR_Gate
endmodule

module F (
  input  D3,
  input  D2,
  input  D1,
  input  D0,
  output out_5
);

  wire and_1_out, and_2_out, and_3_out;

  and and_1 (and_1_out, ~D3, ~D1);  // AND_Gate
  and and_2 (and_2_out, D3, D1);
  and and_3 (and_3_out, D1, ~D0);  // AND_Gate
  or or_1 (out_5, D2, and_1_out, and_2_out, and_3_out);
endmodule

module G (
  input  D3,
  input  D2,
  input  D1,
  input  D0,
  output out_5
);

  wire and_1_out, and_2_out, and_3_out;

  and and_1 (and_1_out, ~D3, ~D1);  // AND_Gate
  and and_2 (and_2_out, ~D3, D0);  // AND_Gate
  and and_3 (and_3_out, D2, D0);
  or or_1 (out_5, and_1_out, and_2_out, and_3_out);
endmodule
