// Logisim project display 7 segmentos(numeros).circ as structural Verilog
module main (
  input  d,
  input  c,
  input  b,
  input  a
);

  wire and_1_out, and_2_out, and_3_out, and_4_out, and_5_out, and_6_out, and_7_out, and_8_out, and_9_out,
       or_1_out, or_2_out, or_3_out, or_4_out, or_5_out, or_6_out, or_7_out, or_8_out;

  and and_1 (and_1_out, ~c, ~a);  // AND_Gate
  and and_2 (and_2_out, c, a);
  and and_3 (and_3_out, ~b, ~a);  // AND_Gate
  and and_4 (and_4_out, b, a);
  and and_5 (and_5_out, ~d, b);  // AND_Gate
  and and_6 (and_6_out, b, ~a);  // AND_Gate
  and and_7 (and_7_out, c, ~b, a);  // AND_Gate
  and and_8 (and_8_out, c, ~b);  // AND_Gate
  and and_9 (and_9_out, c, ~a);  // AND_Gate
  or or_1 (or_1_out, and_5_out, and_1_out, and_6_out, and_7_out);
  or or_2 (or_2_out, d, b, and_1_out, and_2_out);
  or or_3 (or_3_out, ~c, and_3_out, and_4_out);  // OR_Gate
  or or_4 (or_4_out, c, ~b, a);  // OR_Gate
  or or_5 (or_5_out, d, or_1_out);
  or or_6 (or_6_out, and_3_out, and_8_out, and_9_out);
  or or_7 (or_7_out, and_8_out, and_9_out, and_5_out, d);
  or or_8 (or_8_out, and_1_out, and_6_out);
  _7_Segment_Display u_7_segment_display_1 (
    .g(or_7_out), .f(or_6_out), .a(or_2_out), .b(or_3_out), .e(or_8_out), .d(or_5_out), .c(or_4_out));  // open: dp

  // Notes on the sheet:
  //   MAIN
endmodule

module aula (
  input  A,
  input  B,
  output out_3,
  output out_4,
  output out_5,
  output out_6
);

  not not_1 (out_3, B);
  and and_1 (out_4, A, B);
  or or_1 (out_5, A, B);
  nor nor_1 (out_6, ~A, ~B);  // NOR_Gate

  // Notes on the sheet:
  //   A: pull=down
endmodule

module ex_1 (
  input  A,
  input  B,
  input  C,
  input  D,
  output out_5
);

  wire or_1_out, or_2_out;

  or or_1 (or_1_out, A, B);
  or or_2 (or_2_out, or_1_out, C);
  or or_3 (out_5, or_2_out, D);
endmodule

module EX2 (
  input  A,
  input  B,
  input  C,
  output out_4
);

  wire and_1_out, nand_1_out, nor_1_out;

  nor nor_1 (nor_1_out, A, C);
  nand nand_1 (nand_1_out, A, B);
  and and_1 (and_1_out, nor_1_out, B);
  or or_1 (out_4, nor_1_out, and_1_out, nand_1_out);

  // Notes on the sheet:
  //   ____
  //   A+C
  //   __
  //   AB
  //   ____
  //   B(A+C)
endmodule
