// Logisim project trabalho M2.circ as structural Verilog: 12 circuits, main circuit main
module main (
  input  [3:0] in_1,
  input  [3:0] in_2,
  input  [2:0] in_3,
  input  in_4,
  input  in_5,
  input  in_6,
  input  in_7,
  output out_8,
  output out_9,
  output [3:0] out_10,
  output out_11
);

  wire displey_de_7_segmentos_1_a, displey_de_7_segmentos_1_b, displey_de_7_segmentos_1_c,
       displey_de_7_segmentos_1_d, displey_de_7_segmentos_1_e, displey_de_7_segmentos_1_f,
       displey_de_7_segmentos_1_g;

  Displey_de_7_segmentos displey_de_7_segmentos_1 (
    .A3(in_4), .A2(in_5), .A1(in_6), .A0(in_7), .A(displey_de_7_segmentos_1_a),
    .B(displey_de_7_segmentos_1_b), .C(displey_de_7_segmentos_1_c), .D(displey_de_7_segmentos_1_d),
    .E(displey_de_7_segmentos_1_e), .F(displey_de_7_segmentos_1_f), .G(displey_de_7_segmentos_1_g),
    .sinal(out_11));
  ULA ula_1 (.A(in_1), .B(in_2), .in_2(in_3), .OF(out_8), .ZF(out_9), .out_5(out_10));
  _7_Segment_Display u_7_segment_display_1 (
    .g(displey_de_7_segmentos_1_g), .f(displey_de_7_segmentos_1_f), .a(displey_de_7_segmentos_1_a),
    .b(displey_de_7_segmentos_1_b), .e(displey_de_7_segmentos_1_e), .d(displey_de_7_segmentos_1_d),
    .c(displey_de_7_segmentos_1_c));  // open: dp

  // Notes on the sheet:
  //   Trabalho M2 Circuitos Digitais
  //   Nome:Rafael da Cunha,Eduardo Mateus Ferreira
endmodule

module DECREMENTADOR (
  input  A3,
  input  A2,
  input  A1,
  input  A0,
  output [3:0] out_5
);

  wire and_1_out, and_2_out, and_3_out, and_4_out, and_5_out, and_6_out, and_7_out, and_8_out, and_9_out,
       and_10_out, and_11_out, and_12_out, not_1_out, not_2_out, not_3_out, not_4_out, not_5_out, not_6_out,
       not_7_out, not_8_out, not_9_out, not_10_out;

  and and_1 (and_1_out, A3, A0);
  and and_2 (and_2_out, A3, A1);
  and and_3 (and_3_out, A3, A2);
  not not_1 (not_1_out, A2);
  not not_2 (not_2_out, A1);
  not not_3 (not_3_out, A0);
  and and_4 (and_4_out, A1, A0);
  not not_4 (not_4_out, A1);
  and and_5 (and_5_out, A2, not_4_out, not_5_out);
  not not_5 (not_5_out, A0);
  not not_6 (not_6_out, A1);
  and and_6 (and_6_out, A3, not_6_out, not_7_out);
  not not_7 (not_7_out, A0);
  and and_7 (and_7_out, A1, not_8_out);
  not not_8 (not_8_out, A0);
  and and_8 (and_8_out, A2, not_9_out);
  not not_9 (not_9_out, A0);
  and and_9 (and_9_out, A3, not_10_out);
  not not_10 (not_10_out, A0);
  or or_1 (out_5[3], and_1_out, and_2_out, and_3_out);
  and and_10 (and_10_out, A2, A0);
  or or_2 (out_5[2], and_10_out, and_11_out, and_12_out);
  and and_11 (and_11_out, A2, A1);
  and and_12 (and_12_out, A3, not_1_out, not_2_out, not_3_out);
  or or_3 (out_5[1], and_4_out, and_5_out, and_6_out);
  or or_4 (out_5[0], and_7_out, and_8_out, and_9_out);
endmodule

module INCREMENTADOR (
  input  A3,
  input  A2,
  input  A1,
  input  A0,
  output [3:0] out_5,
  output C_out
);

  wire and_2_out, and_3_out, and_4_out, and_5_out, and_6_out, and_7_out, and_8_out, and_9_out, and_10_out,
       not_1_out, not_2_out, not_3_out, not_4_out, not_5_out, not_6_out, not_7_out, not_8_out, not_9_out;

  not not_1 (not_1_out, A3);
  not not_2 (not_2_out, A2);
  not not_3 (not_3_out, A1);
  not not_4 (not_4_out, A0);
  not not_5 (not_5_out, A2);
  not not_6 (not_6_out, A1);
  not not_7 (not_7_out, A0);
  not not_8 (not_8_out, A1);
  not not_9 (not_9_out, A0);
  not not_10 (out_5[0], A0);
  and and_1 (C_out, A3, A2, A1, A0);
  and and_2 (and_2_out, not_1_out, A2, A1, A0);
  and and_3 (and_3_out, A3, not_2_out);
  and and_4 (and_4_out, A3, not_3_out);
  and and_5 (and_5_out, A3, not_4_out);
  and and_6 (and_6_out, not_5_out, A1, A0);
  and and_7 (and_7_out, A2, not_6_out);
  and and_8 (and_8_out, A2, not_7_out);
  and and_9 (and_9_out, not_8_out, A0);
  and and_10 (and_10_out, A1, not_9_out);
  or or_1 (out_5[3], and_2_out, and_3_out, and_4_out, and_5_out);
  or or_2 (out_5[2], and_6_out, and_7_out, and_8_out);
  or or_3 (out_5[1], and_9_out, and_10_out);
endmodule

module \Adição  (
  input  in_1,
  input  in_2,
  output out_3,
  output out_4
);

  and and_1 (out_3, in_1, in_2);
  xor xor_1 (out_4, in_2, in_1);
endmodule

module \Adição_2  (
  input  A,
  input  B,
  input  C_in,
  output C_out,
  output sum
);

  wire \adição_1_out_3 , \adição_1_out_4 , \adição_2_out_3 ;

  \Adição  \adição_1  (.in_1(A), .in_2(B), .out_3(\adição_1_out_3 ), .out_4(\adição_1_out_4 ));
  \Adição  \adição_2  (.in_1(\adição_1_out_4 ), .in_2(C_in), .out_3(\adição_2_out_3 ), .out_4(sum));
  or or_1 (C_out, \adição_1_out_3 , \adição_2_out_3 );
endmodule

module \Adição_3  (
  input  [3:0] a,
  input  [3:0] b,
  input  in_3,
  output out_4,
  output [3:0] out_5
);

  wire \adição_2_2_c_out , \adição_2_3_c_out , \adição_2_4_c_out ;

  \Adição_2  \adição_2_1  (.A(a[3]), .B(b[3]), .C_in(\adição_2_2_c_out ), .C_out(out_4), .sum(out_5[3]));
  \Adição_2  \adição_2_2  (.A(a[2]), .B(b[2]), .C_in(\adição_2_3_c_out ), .C_out(\adição_2_2_c_out ), .sum(out_5[2]));
  \Adição_2  \adição_2_3  (.A(a[1]), .B(b[1]), .C_in(\adição_2_4_c_out ), .C_out(\adição_2_3_c_out ), .sum(out_5[1]));
  \Adição_2  \adição_2_4  (.A(a[0]), .B(b[0]), .C_in(in_3), .C_out(\adição_2_4_c_out ), .sum(out_5[0]));
endmodule

module \subtração  (
  input  [3:0] a,
  input  [3:0] b,
  output out_3,
  output [3:0] out_4
);

  wire \adição_2_2_c_out , \adição_2_3_c_out , \adição_2_4_c_out , not_1_out, not_2_out, not_3_out, not_4_out;

  not not_1 (not_1_out, b[0]);
  not not_2 (not_2_out, b[1]);
  not not_3 (not_3_out, b[2]);
  not not_4 (not_4_out, b[3]);
  \Adição_2  \adição_2_1  (.A(a[3]), .B(not_4_out), .C_in(\adição_2_2_c_out ), .C_out(out_3), .sum(out_4[3]));
  \Adição_2  \adição_2_2  (
    .A(a[2]), .B(not_3_out), .C_in(\adição_2_3_c_out ), .C_out(\adição_2_2_c_out ), .sum(out_4[2]));
  \Adição_2  \adição_2_3  (
    .A(a[1]), .B(not_2_out), .C_in(\adição_2_4_c_out ), .C_out(\adição_2_3_c_out ), .sum(out_4[1]));
  \Adição_2  \adição_2_4  (.A(a[0]), .B(not_1_out), .C_in(1'b1), .C_out(\adição_2_4_c_out ), .sum(out_4[0]));

  // Notes on the sheet:
  //   a
endmodule

module \not  (
  input  [3:0] in_1,
  output [3:0] out_2
);

  assign out_2 = ~in_1;  // NOT_Gate not_1, 4 bits wide
endmodule

module \or  (
  input  [3:0] A,
  input  [3:0] B,
  output [3:0] out_3
);

  assign out_3 = A | B;  // OR_Gate or_1, 4 bits wide
endmodule

module \and  (
  input  [3:0] A,
  input  [3:0] B,
  output [3:0] out_3
);

  assign out_3 = A & B;  // AND_Gate and_1, 4 bits wide
endmodule

module Displey_de_7_segmentos (
  input  A3,
  input  A2,
  input  A1,
  input  A0,
  output A,
  output B,
  output C,
  output D,
  output E,
  output F,
  output G,
  output sinal
);

  wire and_1_out, and_2_out, and_3_out, and_4_out, and_5_out, and_6_out, and_7_out, and_8_out, and_9_out,
       and_10_out, and_11_out, and_12_out, and_13_out, and_14_out, and_15_out, and_16_out, and_17_out,
       and_18_out, and_19_out, and_20_out, and_21_out, and_22_out, and_23_out, and_24_out, and_25_out,
       and_26_out, not_1_out, not_2_out, not_3_out, not_4_out, not_5_out, not_6_out, not_7_out, not_8_out,
       not_9_out, not_10_out, not_11_out, not_12_out, not_13_out, not_14_out, not_15_out, not_16_out,
       not_17_out, not_18_out, not_19_out, not_20_out, not_21_out, not_22_out, not_23_out, not_24_out,
       not_25_out, not_26_out, not_27_out, not_28_out, not_29_out, not_30_out, not_31_out, not_32_out,
       not_33_out, not_34_out, not_35_out;

  not not_1 (not_1_out, A2);
  and and_1 (and_1_out, not_1_out, not_2_out);
  not not_2 (not_2_out, A0);
  not not_3 (not_3_out, A3);
  and and_2 (and_2_out, not_3_out, A1);
  and and_3 (and_3_out, A1, not_4_out);
  not not_4 (not_4_out, A0);
  and and_4 (and_4_out, A2, not_5_out, A0);
  not not_5 (not_5_out, A1);
  and and_5 (and_5_out, A3, not_6_out);
  not not_6 (not_6_out, A2);
  not not_7 (not_7_out, A3);
  and and_6 (and_6_out, not_7_out, not_8_out);
  not not_8 (not_8_out, A2);
  not not_9 (not_9_out, A2);
  and and_7 (and_7_out, not_9_out, not_10_out);
  not not_10 (not_10_out, A1);
  not not_11 (not_11_out, A1);
  and and_8 (and_8_out, not_11_out, not_12_out);
  not not_12 (not_12_out, A0);
  not not_13 (not_13_out, A3);
  and and_9 (and_9_out, not_13_out, A1, A0);
  and and_10 (and_10_out, A3, A2);
  not not_14 (not_14_out, A1);
  not not_15 (not_15_out, A3);
  and and_11 (and_11_out, not_15_out, A2);
  and and_12 (and_12_out, A3, not_16_out);
  not not_16 (not_16_out, A2);
  not not_17 (not_17_out, A2);
  and and_13 (and_13_out, not_17_out, not_18_out);
  not not_18 (not_18_out, A0);
  not not_19 (not_19_out, A2);
  and and_14 (and_14_out, not_19_out, A1);
  and and_15 (and_15_out, A1, not_20_out);
  not not_20 (not_20_out, A0);
  and and_16 (and_16_out, A2, not_21_out, A0);
  not not_21 (not_21_out, A1);
  not not_22 (not_22_out, A2);
  and and_17 (and_17_out, not_22_out, not_23_out);
  not not_23 (not_23_out, A0);
  and and_18 (and_18_out, A1, not_24_out);
  not not_24 (not_24_out, A0);
  not not_25 (not_25_out, A1);
  and and_19 (and_19_out, not_25_out, not_26_out);
  not not_26 (not_26_out, A0);
  not not_27 (not_27_out, A3);
  and and_20 (and_20_out, not_27_out, A2, not_28_out);
  not not_28 (not_28_out, A1);
  not not_29 (not_29_out, A3);
  and and_21 (and_21_out, not_29_out, A2, not_30_out);
  not not_30 (not_30_out, A0);
  and and_22 (and_22_out, A3, not_31_out, A1);
  not not_31 (not_31_out, A2);
  not not_32 (not_32_out, A2);
  and and_23 (and_23_out, not_32_out, A1);
  and and_24 (and_24_out, A2, not_33_out);
  not not_33 (not_33_out, A1);
  and and_25 (and_25_out, A2, not_34_out);
  not not_34 (not_34_out, A0);
  and and_26 (and_26_out, A3, not_35_out);
  not not_35 (not_35_out, A0);
  or or_1 (A, and_1_out, and_2_out, and_3_out, and_4_out, and_5_out);
  or or_2 (B, and_6_out, and_7_out, and_8_out, and_9_out, and_10_out);
  or or_3 (C, not_14_out, A0, and_11_out, and_12_out);
  or or_4 (D, and_13_out, and_14_out, and_15_out, and_16_out);
  or or_5 (E, and_17_out, and_18_out);
  or or_6 (F, and_19_out, and_20_out, and_21_out, and_22_out);
  or or_7 (G, and_23_out, and_24_out, and_25_out, and_26_out);

  assign sinal = A3;
endmodule

module ULA (
  input  [3:0] A,
  input  [2:0] in_2,
  input  [3:0] B,
  output OF,
  output [3:0] out_5,
  output ZF
);

  wire \adição_3_1_out_4 , incrementador_1_c_out, \subtração_1_out_3 ;
  wire [3:0] \adição_3_1_out_5 , and_1_out_3, decrementador_1_out_5, incrementador_1_out_5, not_1_out_2,
       or_1_out_3, \subtração_1_out_4 ;

  INCREMENTADOR incrementador_1 (
    .A3(A[3]), .A2(A[2]), .A1(A[1]), .A0(A[0]), .C_out(incrementador_1_c_out), .out_5(incrementador_1_out_5));
  \Adição_3  \adição_3_1  (.b(B), .out_4(\adição_3_1_out_4 ), .out_5(\adição_3_1_out_5 ), .a(A), .in_3(1'b0));
  DECREMENTADOR decrementador_1 (.A3(A[3]), .A2(A[2]), .A1(A[1]), .A0(A[0]), .out_5(decrementador_1_out_5));
  \subtração  \subtração_1  (.b(B), .out_3(\subtração_1_out_3 ), .out_4(\subtração_1_out_4 ), .a(A));
  \not  not_1 (.in_1(A), .out_2(not_1_out_2));
  \or  or_1 (.A(A), .B(B), .out_3(or_1_out_3));
  \and  and_1 (.A(A), .B(B), .out_3(and_1_out_3));
  Multiplexer #(.select(3), .width(4), .enable("false")) multiplexer_1 (
    .in0(A), .in1(decrementador_1_out_5), .in2(incrementador_1_out_5), .in3(\adição_3_1_out_5 ),
    .in4(\subtração_1_out_4 ), .in5(not_1_out_2), .in6(or_1_out_3), .in7(and_1_out_3), .out(out_5), .sel(in_2));
  nor nor_1 (ZF, out_5[0], out_5[1], out_5[2], out_5[3]);
  Multiplexer #(.select(3), .enable("false")) multiplexer_2 (
    .in0(1'b0), .in1(1'b0), .in2(incrementador_1_c_out), .in3(\adição_3_1_out_4 ), .in4(\subtração_1_out_3 ),
    .in5(1'b0), .in6(1'b0), .in7(1'b0), .out(OF), .sel(in_2));
endmodule
