// Logisim project trabalho M3.circ as structural Verilog: 4 circuits, main circuit main
module main (
  output [3:0] out_1
);

  wire button_1_out, clock_1_out;

  Clock clock_1 (.out(clock_1_out));
  Button button_1 (.out(button_1_out));
  \junção  \junção_1  (.clock(clock_1_out), .clear(button_1_out), .out_3(out_1));
  Hex_Digit_Display hex_digit_display_1 (.value(out_1));  // open: dp

  // Notes on the sheet:
  //   2 seguencia:Extra:12,13,7,9,11,10,6,3,1,14
  //   TRABALHO M3
  //   Nome: Rafael da Cunha
  //   1 seguencia:Rafael da Cunha:9,14,15,10,2,3,8,13,6,12.
endmodule

module FF_MEU (
  input  in_1,
  input  in_2,
  output [3:0] out_3,
  output out_4
);

  wire and_1_out, and_2_out, and_3_out, and_4_out, and_5_out, and_6_out, and_7_out, and_8_out, and_9_out,
       and_10_out, and_11_out, and_12_out, and_13_out, and_14_out, and_15_out, and_16_out, d_ff_1_qn,
       not_1_out, not_2_out, not_3_out, not_4_out, not_5_out, not_6_out, not_7_out, not_8_out, not_9_out,
       not_10_out, not_11_out, not_12_out, not_13_out, not_14_out, not_15_out, not_16_out, not_17_out,
       not_18_out, not_19_out, not_20_out, not_21_out, not_22_out, or_1_out, or_2_out, or_3_out, or_4_out;

  not not_1 (not_1_out, out_3[3]);
  not not_2 (not_2_out, out_3[1]);
  not not_3 (not_3_out, out_3[1]);
  not not_4 (not_4_out, out_3[0]);
  not not_5 (not_5_out, out_3[2]);
  not not_6 (not_6_out, out_3[0]);
  not not_7 (not_7_out, out_3[2]);
  not not_8 (not_8_out, out_3[1]);
  not not_9 (not_9_out, out_3[1]);
  not not_10 (not_10_out, out_3[2]);
  not not_11 (not_11_out, out_3[0]);
  not not_12 (not_12_out, out_3[1]);
  not not_13 (not_13_out, out_3[3]);
  not not_14 (not_14_out, out_3[2]);
  not not_15 (not_15_out, out_3[0]);
  not not_16 (not_16_out, out_3[3]);
  not not_17 (not_17_out, out_3[1]);
  not not_18 (not_18_out, out_3[1]);
  not not_19 (not_19_out, out_3[0]);
  not not_20 (not_20_out, out_3[3]);
  not not_21 (not_21_out, out_3[2]);
  not not_22 (not_22_out, out_3[0]);
  and and_1 (and_1_out, not_1_out, not_2_out);
  and and_2 (and_2_out, not_3_out, not_4_out);
  and and_3 (and_3_out, not_5_out, out_3[0]);
  and and_4 (and_4_out, out_3[2], out_3[1]);
  and and_5 (and_5_out, out_3[2], out_3[1], not_6_out);
  and and_6 (and_6_out, out_3[3], not_7_out, not_8_out);
  and and_7 (and_7_out, out_3[3], not_9_out, out_3[0]);
  and and_8 (and_8_out, not_10_out, out_3[1], not_11_out);
  and and_9 (and_9_out, out_3[3], not_12_out, out_3[0]);
  and and_10 (and_10_out, out_3[3], out_3[2], out_3[1]);
  and and_11 (and_11_out, not_13_out, not_14_out, not_15_out);
  and and_12 (and_12_out, not_16_out, not_17_out);
  and and_13 (and_13_out, not_18_out, not_19_out);
  and and_14 (and_14_out, not_20_out, out_3[2], out_3[0]);
  and and_15 (and_15_out, out_3[3], not_21_out, out_3[1], out_3[0]);
  and and_16 (and_16_out, out_3[3], out_3[2], not_22_out);
  or or_1 (or_1_out, and_1_out, and_2_out, and_3_out, and_4_out);
  or or_2 (or_2_out, and_5_out, and_6_out, and_7_out);
  or or_3 (or_3_out, and_8_out, and_9_out, and_10_out);
  or or_4 (or_4_out, and_11_out, and_12_out, and_13_out, and_14_out, and_15_out, and_16_out);
  D_Flip_Flop d_ff_1 (.clk(in_2), .D(or_1_out), .Q(out_3[3]), .Qn(d_ff_1_qn), .reset(in_1));  // open: preset, en
  D_Flip_Flop d_ff_2 (.clk(in_2), .D(or_2_out), .Q(out_3[2]), .reset(in_1));  // open: Qn, preset, en
  D_Flip_Flop d_ff_3 (.clk(in_2), .D(or_3_out), .Q(out_3[1]), .reset(in_1));  // open: Qn, preset, en
  D_Flip_Flop d_ff_4 (.clk(in_2), .D(or_4_out), .Q(out_3[0]), .reset(in_1));  // open: Qn, preset, en
  Hex_Digit_Display hex_digit_display_1 (.value(out_3));  // open: dp
  and and_17 (out_4, out_3[3], out_3[2], ~out_3[1], ~out_3[0]);  // AND_Gate

  // Notes on the sheet:
  //   Rafael da Cunha:9,14,15,10,2,3,8,13,6,12.
endmodule

module FF_EXTRA (
  input  in_1,
  input  in_2,
  output [3:0] out_3,
  output out_4
);

  wire and_1_out, and_2_out, and_3_out, and_4_out, and_5_out, and_6_out, and_7_out, and_8_out, and_9_out,
       and_10_out, and_11_out, and_12_out, and_13_out, and_14_out, and_15_out, and_16_out, and_17_out,
       not_1_out, not_2_out, not_3_out, not_4_out, not_5_out, not_6_out, not_7_out, not_8_out, not_9_out,
       not_10_out, not_11_out, not_12_out, not_13_out, not_14_out, not_15_out, not_16_out, not_17_out,
       not_18_out, not_19_out, not_20_out, not_21_out, not_22_out, not_23_out, or_1_out, or_2_out, or_3_out,
       or_4_out;

  not not_1 (not_1_out, out_3[3]);
  not not_2 (not_2_out, out_3[2]);
  not not_3 (not_3_out, out_3[0]);
  not not_4 (not_4_out, out_3[3]);
  not not_5 (not_5_out, out_3[1]);
  not not_6 (not_6_out, out_3[2]);
  not not_7 (not_7_out, out_3[1]);
  not not_8 (not_8_out, out_3[3]);
  not not_9 (not_9_out, out_3[0]);
  not not_10 (not_10_out, out_3[3]);
  not not_11 (not_11_out, out_3[1]);
  not not_12 (not_12_out, out_3[2]);
  not not_13 (not_13_out, out_3[0]);
  not not_14 (not_14_out, out_3[2]);
  not not_15 (not_15_out, out_3[1]);
  not not_16 (not_16_out, out_3[3]);
  not not_17 (not_17_out, out_3[0]);
  not not_18 (not_18_out, out_3[1]);
  not not_19 (not_19_out, out_3[2]);
  not not_20 (not_20_out, out_3[3]);
  not not_21 (not_21_out, out_3[3]);
  not not_22 (not_22_out, out_3[1]);
  not not_23 (not_23_out, out_3[1]);
  and and_1 (and_1_out, not_1_out, not_2_out, not_3_out);
  and and_2 (and_2_out, not_4_out, not_5_out);
  and and_3 (and_3_out, not_6_out, not_7_out);
  and and_4 (and_4_out, not_8_out, out_3[2], out_3[0]);
  and and_5 (and_5_out, out_3[3], out_3[1], out_3[0]);
  and and_6 (and_6_out, out_3[3], out_3[2], not_9_out);
  and and_7 (and_7_out, not_10_out, not_11_out);
  and and_8 (and_8_out, not_12_out, not_13_out);
  and and_9 (and_9_out, out_3[3], out_3[2]);
  and and_10 (and_10_out, not_14_out, not_15_out, out_3[0]);
  and and_11 (and_11_out, not_16_out, out_3[2], out_3[1], not_17_out);
  and and_12 (and_12_out, out_3[3], not_18_out, out_3[0]);
  and and_13 (and_13_out, out_3[3], not_19_out, out_3[1]);
  and and_14 (and_14_out, not_20_out, out_3[1], out_3[0]);
  and and_15 (and_15_out, not_21_out, out_3[2], out_3[1]);
  and and_16 (and_16_out, out_3[3], not_22_out, out_3[0]);
  and and_17 (and_17_out, out_3[3], out_3[2], not_23_out);
  or or_1 (or_1_out, and_1_out, and_2_out, and_3_out, and_4_out, and_5_out, and_6_out);
  or or_2 (or_2_out, and_7_out, and_8_out, and_9_out);
  or or_3 (or_3_out, and_10_out, and_11_out, and_12_out, and_13_out);
  or or_4 (or_4_out, and_14_out, and_15_out, and_16_out, and_17_out);
  D_Flip_Flop d_ff_1 (.clk(in_1), .D(or_1_out), .Q(out_3[3]), .reset(in_2));  // open: Qn, preset, en
  D_Flip_Flop d_ff_2 (.clk(in_1), .D(or_2_out), .Q(out_3[2]), .reset(in_2));  // open: Qn, preset, en
  D_Flip_Flop d_ff_3 (.clk(in_1), .D(or_3_out), .Q(out_3[1]), .reset(in_2));  // open: Qn, preset, en
  D_Flip_Flop d_ff_4 (.clk(in_1), .D(or_4_out), .Q(out_3[0]), .reset(in_2));  // open: Qn, preset, en
  Hex_Digit_Display hex_digit_display_1 (.value(out_3));  // open: dp
  and and_18 (out_4, out_3[3], out_3[2], out_3[1], ~out_3[0]);  // AND_Gate

  // Notes on the sheet:
  //   Extra:12,13,7,9,11,10,6,3,1,14
endmodule

module \junção  (
  input  clock,
  input  clear,
  output [3:0] out_3
);

  wire and_1_out, ff_extra_1_out_4, ff_meu_1_out_4, j_k_ff_1_q;
  wire [3:0] ff_extra_1_out_3, ff_meu_1_out_3;

  FF_MEU ff_meu_1 (.in_2(clock), .out_3(ff_meu_1_out_3), .out_4(ff_meu_1_out_4), .in_1(clear));
  FF_EXTRA ff_extra_1 (.out_3(ff_extra_1_out_3), .in_1(clock), .out_4(ff_extra_1_out_4), .in_2(clear));
  and and_1 (and_1_out, ff_meu_1_out_4, ff_extra_1_out_4);
  Multiplexer #(.width(4), .enable("false")) multiplexer_1 (
    .in0(ff_meu_1_out_3), .in1(ff_extra_1_out_3), .out(out_3), .sel(j_k_ff_1_q));
  J_K_Flip_Flop j_k_ff_1 (.J(and_1_out), .clk(clock), .K(and_1_out), .Q(j_k_ff_1_q));  // open: Qn, preset, en, reset
  Hex_Digit_Display hex_digit_display_1 (.value(out_3));  // open: dp
endmodule
